# Fritzing sketch edison_schematics (saved by Fritzing 0.9.3b)
breadboards: 1

parts:
  Part3 = Adafruit_BMP280
  Part4 = 0.56" 7-segment LED Backpack [part_number=881]
  S2 = Pushbutton [package="[THT]"]
  R1 = Resistor [tolerance=±5% resistance=10k package="2512 [SMD]"]
  Part5 = Intel Edison Arduinobreakout

nets:
  VIN: Part3.VIN, Part4.VDD, R1.Pin_0, Part5.5V
  GND: Part3.GND, Part4.GND, S2.Pin_1, S2.Pin_2, Part5.GND
  N1: Part3.SCK/SCL, Part4.SCL, Part5.A5/SCL
  N2: Part3.SDI/SDA, Part4.SDA, Part5.A4/SDA
  N3: S2.Pin_3, S2.Pin_4, R1.Pin_1, Part5.D12/MISO

custom parts:
  Adafruit_BMP280: Bosch has stepped up their game with their new BMP280 sensor, an environmental sensor with temperature, barometric pressure that is the next generation upgrade to the BMP085/BMP180/BMP183. This sensor is great for all sorts of weather sensing and can even be used in both I2C and SPI! This precision sensor from Bosch is the best low-cost, precision sensing solution for measuring barometric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
  0.56" 7-segment LED Backpack: This 0.56" 7-segment LED display includes a driver chip for simple control via an I2C interface. The backpack features address-selection jumpers so you can connect up to eight displays on a single I2C bus.
